// Logisim project circuito.circ as structural Verilog: 1 circuit, main circuit main
module main (
  input  A,
  input  B,
  input  C,
  input  D
);

  wire and_1_out, and_2_out, and_3_out, and_4_out, xor_1_out;

  and and_1 (and_1_out, A, B);
  and and_2 (and_2_out, A, xor_1_out);
  LED led_1 (.in(and_2_out));
  and and_3 (and_3_out, A, C);
  ExactlyOne xor_1 (.out(xor_1_out), .in0(and_1_out), .in1(and_3_out), .in2(and_4_out));
  and and_4 (and_4_out, A, D);
endmodule
